// Logisim project fsmSemaforo.circ as structural Verilog: 1 circuit, main circuit main
module main (
  input  rst
);

  wire and_1_out, and_2_out, and_3_out, clk_out, m_out, not_1_out, or_1_out, or_2_out, q0_q, q0_qn, q1_q,
       q1_qn, rgbled_1_p2;

  Button m (.out(m_out));
  Clock clk (.out(clk_out));
  not not_1 (not_1_out, m_out);
  and and_1 (and_1_out, m_out, q1_qn);
  and and_2 (and_2_out, not_1_out, q0_q);
  and and_3 (and_3_out, m_out, q1_q);
  D_Flip_Flop q1 (.D(or_1_out), .clk(clk_out), .Q(q1_q), .Qn(q1_qn), .preset(rst));  // open: reset
  or or_1 (or_1_out, q0_qn, and_1_out);
  D_Flip_Flop q0 (.D(or_2_out), .clk(clk_out), .Q(q0_q), .Qn(q0_qn), .reset(rst));  // open: preset
  or or_2 (or_2_out, and_2_out, and_3_out);
  // RGBLED rgbled_1: pin names not known; wires that end beside it: q0_q, rgbled_1_p2
  or or_3 (rgbled_1_p2, q1_q, q0_qn);
endmodule
