// Logisim project 0006_Q4.circ as structural Verilog: 11 circuits, main circuit contador
module contador (
  input  rst_n,
  input  cgp,
  input  cnt,
  input  clk,
  input  [3:0] e,
  output max,
  output [3:0] s
);

  wire not_1_out;

  Counter #(.width(4), .max('hf)) counter_1 (
    .clr(not_1_out), .load(cgp), .up(1'b1), .count(cnt), .clk(clk), .D(e), .carry(max), .Q(s));
  not not_1 (not_1_out, rst_n);
endmodule

module P1 (
);

  wire and_1_out, and_2_out, clk_out;
  wire [3:0] C0_s, C1_s;

  Clock clk (.out(clk_out));
  contador C1 (.rst_n(1'b1), .cgp(and_1_out), .cnt(and_2_out), .clk(clk_out), .e(4'b1110), .s(C1_s));  // open: max
  contador C0 (.rst_n(1'b1), .cgp(and_2_out), .cnt(1'b1), .clk(clk_out), .e(4'b0010), .s(C0_s));  // open: max
  and and_1 (and_1_out, C1_s[0], C1_s[1], ~C1_s[2], ~C1_s[3], and_2_out);  // AND_Gate
  and and_2 (and_2_out, C0_s[0], ~C0_s[1], ~C0_s[2], C0_s[3]);  // AND_Gate
  Hex_Digit_Display hex_digit_display_1 (.value(C0_s));  // open: dp
  Hex_Digit_Display hex_digit_display_2 (.value(C1_s));  // open: dp

  // Notes on the sheet:
  //   0x
  //   0x
  //   D1
  //   D0
endmodule

module P2 (
  input  cnt
);

  wire C0_max, clk_out;
  wire [3:0] C0_s, C1_s;

  Clock clk (.out(clk_out));
  contador C1 (.rst_n(1'b1), .cgp(1'b0), .cnt(C0_max), .clk(clk_out), .s(C1_s));  // open: e, max
  contador C0 (.rst_n(1'b1), .cgp(C0_max), .cnt(cnt), .clk(clk_out), .e(4'b1110), .max(C0_max), .s(C0_s));
  Hex_Digit_Display hex_digit_display_1 (.value(C0_s));  // open: dp
  Hex_Digit_Display hex_digit_display_2 (.value(C1_s));  // open: dp

  // Notes on the sheet:
  //   0x
  //   D0
  //   D1
endmodule

module P3 (
);

  wire and_1_out, and_2_out, clk_out;
  wire [3:0] C0_s, C1_s;

  Clock clk (.out(clk_out));
  contador C1 (.rst_n(1'b1), .cgp(and_1_out), .cnt(and_2_out), .clk(clk_out), .e(4'b1010), .s(C1_s));  // open: max
  contador C0 (.rst_n(1'b1), .cgp(and_2_out), .cnt(1'b1), .clk(clk_out), .e(4'b0111), .s(C0_s));  // open: max
  and and_1 (and_1_out, ~C1_s[0], ~C1_s[1], C1_s[2], C1_s[3], and_2_out);  // AND_Gate
  and and_2 (and_2_out, C0_s[0], ~C0_s[1], ~C0_s[2], C0_s[3]);  // AND_Gate
  Hex_Digit_Display hex_digit_display_1 (.value(C1_s));  // open: dp
  Hex_Digit_Display hex_digit_display_2 (.value(C0_s));  // open: dp

  // Notes on the sheet:
  //   0x
  //   0x
  //   D1
  //   D0
endmodule

module P4 (
);

  wire and_1_out, and_2_out, clk_out;
  wire [3:0] C0_s, C1_s;

  Clock clk (.out(clk_out));
  contador C1 (.rst_n(1'b1), .cgp(and_1_out), .cnt(and_2_out), .clk(clk_out), .e(4'b0000), .s(C1_s));  // open: max
  contador C0 (.rst_n(1'b1), .cgp(and_2_out), .cnt(1'b1), .clk(clk_out), .e(4'b1101), .s(C0_s));  // open: max
  and and_1 (and_1_out, C1_s[0], C1_s[1], ~C1_s[2], ~C1_s[3], and_2_out);  // AND_Gate
  and and_2 (and_2_out, C0_s[0], C0_s[1], C0_s[2], C0_s[3]);
  Hex_Digit_Display hex_digit_display_1 (.value(C1_s));  // open: dp
  Hex_Digit_Display hex_digit_display_2 (.value(C0_s));  // open: dp

  // Notes on the sheet:
  //   0x
  //   0x
  //   D0
  //   D1
endmodule

module P5 (
);

  wire and_1_out, clk_out;
  wire [3:0] C0_s, C1_s;

  Clock clk (.out(clk_out));
  contador C1 (.rst_n(1'b1), .cgp(1'b0), .cnt(and_1_out), .clk(clk_out), .e(4'b1010), .s(C1_s));  // open: max
  contador C0 (.rst_n(1'b1), .cgp(and_1_out), .cnt(1'b1), .clk(clk_out), .e(4'b0010), .s(C0_s));  // open: max
  and and_1 (and_1_out, C0_s[0], ~C0_s[1], C0_s[2], ~C0_s[3]);  // AND_Gate
  Hex_Digit_Display hex_digit_display_1 (.value(C0_s));  // open: dp
  Hex_Digit_Display hex_digit_display_2 (.value(C1_s));  // open: dp

  // Notes on the sheet:
  //   0x
  //   0x
  //   D0
  //   D1
endmodule

module P6 (
);

  wire and_1_out, and_2_out, clk_out;
  wire [3:0] contador_1_s, contador_2_s;

  Clock clk (.out(clk_out));
  contador contador_1 (
    .rst_n(1'b1), .cgp(and_1_out), .cnt(1'b1), .clk(and_2_out), .e(4'b1110), .s(contador_1_s));  // open: max
  contador contador_2 (
    .rst_n(1'b1), .cgp(and_2_out), .cnt(1'b1), .clk(clk_out), .e(4'b0010), .s(contador_2_s));  // open: max
  and and_1 (and_1_out, contador_1_s[0], contador_1_s[1], ~contador_1_s[2], ~contador_1_s[3], and_2_out);  // AND_Gate
  and and_2 (and_2_out, contador_2_s[0], contador_2_s[1], ~contador_2_s[2], ~contador_2_s[3]);  // AND_Gate
  Hex_Digit_Display hex_digit_display_1 (.value(contador_2_s));  // open: dp
  Hex_Digit_Display hex_digit_display_2 (.value(contador_1_s));  // open: dp

  // Notes on the sheet:
  //   0x
  //   0x
  //   C1
  //   C0
  //   D1
  //   D0
endmodule

module P7 (
);

  wire and_1_out, clock_1_out, nand_1_out;
  wire [3:0] contador_1_s, contador_2_s;

  Clock clock_1 (.out(clock_1_out));
  contador contador_1 (
    .rst_n(nand_1_out), .cgp(1'b0), .cnt(1'b1), .clk(and_1_out), .e(4'b1110), .s(contador_1_s));  // open: max
  contador contador_2 (
    .rst_n(1'b1), .cgp(and_1_out), .cnt(1'b1), .clk(clock_1_out), .e(4'b1010), .s(contador_2_s));  // open: max
  nand nand_1 (nand_1_out, contador_1_s[0], contador_1_s[1], ~contador_1_s[2], ~contador_1_s[3], and_1_out);  // NAND_Gate
  and and_1 (and_1_out, contador_2_s[0], contador_2_s[1], ~contador_2_s[2], contador_2_s[3]);  // AND_Gate
  Hex_Digit_Display hex_digit_display_1 (.value(contador_1_s));  // open: dp
  Hex_Digit_Display hex_digit_display_2 (.value(contador_2_s));  // open: dp

  // Notes on the sheet:
  //   clk
  //   0x
  //   0x
  //   C1
  //   C0
  //   D0
  //   D1
endmodule

module P8 (
);

  wire and_1_out, clock_1_out, nand_1_out;
  wire [3:0] contador_1_s, contador_2_s;

  Clock clock_1 (.out(clock_1_out));
  contador contador_1 (
    .rst_n(nand_1_out), .cgp(1'b0), .cnt(1'b1), .clk(and_1_out), .e(4'b0001), .s(contador_1_s));  // open: max
  contador contador_2 (
    .rst_n(1'b1), .cgp(and_1_out), .cnt(1'b1), .clk(clock_1_out), .e(4'b1010), .s(contador_2_s));  // open: max
  nand nand_1 (nand_1_out, contador_1_s[0], contador_1_s[1], ~contador_1_s[2], ~contador_1_s[3]);  // NAND_Gate
  and and_1 (and_1_out, contador_2_s[0], contador_2_s[1], ~contador_2_s[3]);  // AND_Gate
  Hex_Digit_Display hex_digit_display_1 (.value(contador_1_s));  // open: dp
  Hex_Digit_Display hex_digit_display_2 (.value(contador_2_s));  // open: dp

  // Notes on the sheet:
  //   clk
  //   0x
  //   0x
  //   C1
  //   C0
  //   D1
  //   D0
endmodule

module P9 (
);

  wire clock_1_out, nand_1_out, nand_2_out;
  wire [3:0] contador_1_s, contador_2_s;

  Clock clock_1 (.out(clock_1_out));
  contador contador_1 (
    .rst_n(nand_1_out), .cgp(1'b0), .cnt(1'b1), .clk(clock_1_out), .e(4'b0001), .s(contador_1_s));  // open: max
  contador contador_2 (
    .rst_n(nand_2_out), .cgp(1'b0), .cnt(1'b1), .clk(clock_1_out), .e(4'b1010), .s(contador_2_s));  // open: max
  nand nand_1 (nand_1_out, contador_1_s[2], ~contador_1_s[0]);  // NAND_Gate
  nand nand_2 (nand_2_out, contador_2_s[0], contador_2_s[1]);
  Hex_Digit_Display hex_digit_display_1 (.value(contador_2_s));  // open: dp
  Hex_Digit_Display hex_digit_display_2 (.value(contador_1_s));  // open: dp

  // Notes on the sheet:
  //   clk
  //   0x
  //   0x
  //   C1
  //   C0
  //   D0
  //   D1
endmodule

module P10 (
);

  wire and_1_out, clock_1_out, nand_1_out;
  wire [3:0] contador_1_s, contador_2_s;

  Clock clock_1 (.out(clock_1_out));
  contador contador_1 (
    .rst_n(nand_1_out), .cgp(1'b0), .cnt(1'b1), .clk(and_1_out), .e(4'b1110), .s(contador_1_s));  // open: max
  contador contador_2 (
    .rst_n(1'b1), .cgp(and_1_out), .cnt(1'b1), .clk(clock_1_out), .e(4'b1010), .s(contador_2_s));  // open: max
  nand nand_1 (nand_1_out, contador_1_s[2], and_1_out);
  and and_1 (and_1_out, contador_2_s[0], contador_2_s[1], ~contador_2_s[2], contador_2_s[3]);  // AND_Gate
  Hex_Digit_Display hex_digit_display_1 (.value(contador_2_s));  // open: dp
  Hex_Digit_Display hex_digit_display_2 (.value(contador_1_s));  // open: dp

  // Notes on the sheet:
  //   clk
  //   0x
  //   0x
  //   C1
  //   C0
  //   D0
  //   D1
endmodule
