// Logisim project 20181009_projFfT.circ as structural Verilog: 1 circuit, main circuit fullReset
module fullReset (
  input  T,
  input  C,
  input  reset,
  output Q
);

  wire and_1_out, nand_1_out, nand_2_out, nand_3_out, nand_4_out, nand_5_out, nand_6_out, nand_7_out,
       nand_8_out, nand_9_out, nand_10_out;

  nand nand_1 (nand_1_out, T, C, Q);
  nand nand_2 (nand_2_out, ~T, ~C, ~Q);  // NAND_Gate
  nand nand_3 (nand_3_out, ~T, ~C, Q);  // NAND_Gate
  nand nand_4 (nand_4_out, T, C, ~Q);  // NAND_Gate
  nand nand_5 (nand_5_out, ~and_1_out, T, ~C);  // NAND_Gate
  nand nand_6 (nand_6_out, and_1_out, T, ~C);  // NAND_Gate
  nand nand_7 (nand_7_out, nand_1_out, nand_2_out, nand_8_out);
  nand nand_8 (nand_8_out, and_1_out, nand_3_out, nand_4_out);
  nand nand_9 (nand_9_out, nand_5_out, nand_10_out);
  nand nand_10 (nand_10_out, Q, nand_6_out);
  and and_1 (and_1_out, nand_7_out, reset);
  and and_2 (Q, nand_9_out, reset);
endmodule
