// Logisim project fsmSemaforo.circ as structural Verilog: 1 circuit, main circuit main
module main (
  input  rst
);

  wire and_1_out, and_2_out, and_3_out, and_4_out, and_5_out, clk_out, m_out, not_1_out, or_1_out, or_2_out,
       or_3_out, q0_q, q0_qn, q1_q, q1_qn;

  Button m (.out(m_out));
  Clock clk (.out(clk_out));
  not not_1 (not_1_out, m_out);
  and and_1 (and_1_out, q1_q, q0_qn);
  and and_2 (and_2_out, q1_qn, m_out, q0_q);
  and and_3 (and_3_out, q1_qn, q0_qn);
  and and_4 (and_4_out, q0_q, not_1_out);
  and and_5 (and_5_out, q1_q, m_out);
  D_Flip_Flop q1 (.D(or_1_out), .clk(clk_out), .Q(q1_q), .Qn(q1_qn), .reset(rst));  // open: preset
  or or_1 (or_1_out, and_1_out, and_2_out);
  D_Flip_Flop q0 (.D(or_2_out), .clk(clk_out), .Q(q0_q), .Qn(q0_qn), .reset(rst));  // open: preset
  or or_2 (or_2_out, and_3_out, and_4_out, and_5_out);
  or or_3 (or_3_out, q1_qn, q0_q);
  // RGBLED rgbled_1: pin names not known; wires that end beside it: or_3_out, q1_q
endmodule
