// Logisim project 20181012_associacaoContadores.circ as structural Verilog: 3 circuits, main circuit main
module main (
  output A,
  output B
);

  wire clock_1_out, nand_1_out;
  wire [3:0] conta_1_outa, contb_1_outb;

  Clock clock_1 (.out(clock_1_out));
  contA conta_1 (.load(A), .clk(clock_1_out), .inA(4'b0101), .outA(conta_1_outa));
  and and_1 (A, conta_1_outa[3], ~conta_1_outa[2], ~conta_1_outa[1], conta_1_outa[0]);  // AND_Gate
  contB contb_1 (.reset_n(nand_1_out), .en(A), .clk(clock_1_out), .outB(contb_1_outb));
  nand nand_1 (nand_1_out, ~contb_1_outb[3], ~contb_1_outb[2], contb_1_outb[1], contb_1_outb[0]);  // NAND_Gate
  and and_2 (B, contb_1_outb[1], ~contb_1_outb[0]);  // AND_Gate
endmodule

module contA (
  input  load,
  input  clk,
  input  [3:0] inA,
  output [3:0] outA
);

  Counter #(.width(4), .max('hf)) counter_1 (
    .clr(1'b0), .load(load), .up(1'b1), .count(1'b1), .clk(clk), .D(inA), .Q(outA));  // open: carry
endmodule

module contB (
  input  reset_n,
  input  en,
  input  clk,
  output [3:0] outB
);

  wire not_1_out;

  not not_1 (not_1_out, reset_n);
  Counter #(.width(4), .max('hf)) counter_1 (
    .clr(not_1_out), .load(1'b0), .up(1'b1), .count(en), .clk(clk), .Q(outB));  // open: D, carry
endmodule
